# Fritzing sketch MeubleTV (saved by Fritzing 0.9.3b)

parts:
  Power_plug2 = Power plug
  LPD8806_RGB_LED_Strip2 = LPD8806 RGB LED Strip
  LPD8806_RGB_LED_Strip3 = LPD8806 RGB LED Strip
  LPD8806_RGB_LED_Strip4 = LPD8806 RGB LED Strip
  Composant2 = Arduino Uno (Rev3) - ICSP
  LPD8806_RGB_LED_Strip1 = LPD8806 RGB LED Strip

nets:
  GND: Power_plug2.GND, LPD8806_RGB_LED_Strip2.GND, LPD8806_RGB_LED_Strip3.GND, LPD8806_RGB_LED_Strip4.GND, Composant2.GND, LPD8806_RGB_LED_Strip1.GND
  +5V: Power_plug2.VCC, LPD8806_RGB_LED_Strip2.+5V, LPD8806_RGB_LED_Strip3.+5V, LPD8806_RGB_LED_Strip4.+5V, Composant2.VIN, LPD8806_RGB_LED_Strip1.+5V
  N1: LPD8806_RGB_LED_Strip2.DI, Composant2.D8
  N2: LPD8806_RGB_LED_Strip2.CI, Composant2.D9_PWM
  N3: LPD8806_RGB_LED_Strip3.DI, Composant2.D6_PWM
  N4: LPD8806_RGB_LED_Strip3.CI, Composant2.D7
  N5: LPD8806_RGB_LED_Strip4.DI, Composant2.D10_PWM/SS
  N6: LPD8806_RGB_LED_Strip4.CI, Composant2.D11_PWM/MOSI
  N7: Composant2.D4, LPD8806_RGB_LED_Strip1.DI
  N8: Composant2.D5_PWM, LPD8806_RGB_LED_Strip1.CI

notes:
  DC 5V 30A
  LedStrip APA102
  UNO R3 + WiFi + ESP8266 USB-TTL CH340G

custom parts:
  LPD8806 RGB LED Strip: Digitally addressable RGB LED strip
